# Fritzing sketch SupplySwitch (saved by Fritzing 0.9.3b)
circuit board: 8.3cm x 8.3cm
breadboards: 1

parts:
  R5 = Resistor [tolerance=±5% resistance=1k package=THT]
  R4 = Resistor [tolerance=±5% resistance=10k package=THT]
  SOFT_OFF = Momentary Switch [package=ksa_sealed_tac_switch]
  LED = LED - 5mm [color="Red (633nm)" package="5 mm [THT]"]
  D2 = Rectifier Diode [part_number=1N4001 package="300 mil [THT]"]
  R2 = Resistor [tolerance=±5% resistance=22k package=THT]
  R1 = Resistor [tolerance=±5% resistance=22k package=THT]
  R3 = Resistor [tolerance=±5% resistance=10k package=THT]
  ON = Momentary Switch [package=ksa_sealed_tac_switch]
  OFF = Momentary Switch [package=ksa_sealed_tac_switch]
  C1 = Electrolytic Capacitor [capacitance=220µF package="300 mil [THT, electrolytic]"]
  R6 = Resistor [tolerance=±5% resistance=1k package=THT]
  P2_-_5V_Out = Header 2 [package=jst-2-pth]
  P1 = Header 2 [package=jst-2-pth]
  Q2 = NPN-Transistor [package="SOT-23 [SMD]"]
  D1 = Rectifier Diode [part_number=1N4001 package="300 mil [THT]"]
  P1_-_5V_In = Header 2 [package=jst-2-pth]
  Relay = songle relay
  Q1 = NPN-Transistor [package="TO92 [THT]"]

nets:
  N1: R5.Pin_0, R4.Pin_0, SOFT_OFF.1, SOFT_OFF.2
  N2: R5.Pin_1, P1.2
  GND: R4.Pin_1, LED.cathode, OFF.3, OFF.4, C1.-, P2_-_5V_Out.1, Q2.2, P1_-_5V_In.1
  N3: SOFT_OFF.3, SOFT_OFF.4, D2.anode, R6.Pin_1, P1.1
  N4: LED.anode, R6.Pin_0
  N5: D2.cathode, R2.Pin_1
  N6: R2.Pin_0, R1.Pin_0, R3.Pin_1, C1.+
  N7: R1.Pin_1, Relay.NC
  N8: R3.Pin_0, OFF.1, OFF.2, Q1.B
  N9: ON.1, ON.2, P1_-_5V_In.2, Relay.COMMON
  N10: ON.3, ON.4, P2_-_5V_Out.2, D1.cathode, Relay.VCC, Relay.NO
  N11: Q2.0, Q1.E
  N12: Q2.1, D1.anode, Relay.GND, Q1.C
